# Fritzing sketch Mega_DHT_LCD (saved by Fritzing 0.9.3b)
breadboards: 1

parts:
  Part1 = Arduino Ethernet Shield (Rev3)
  Part2 = Arduino Mega ADK (Rev3)
  Part3 = Adafruit Micro USB Breakout [part_number="Adafruit #1833"]
  F1 = Fan - Ventilador [package=THT]
  LCD1 = LCD screen  # not connected
  LCM1602_IIC1 = LCM1602 IIC [part_number="LCM1602 IIC" chip_label="LCM1602 IIC" package="DIP (Dual Inline) [THT]"]
  KF-1 = KF-301 Relay [package=THT]
  S1 = Pushbutton [package="[SMD]"]
  Mod1 = KY-015 Temperature & Humidity Sensor Module [package="Breakout board"]
  LED1 = smd LED [color="Red (633nm)" package="0805 [SMD]"]

nets:
  N1: Part1.D8, KF-1.signal
  N2: Part1.PWM_D9, LED1.anode
  GND: Part1.GND, Part3.GND, F1.GND, LCM1602_IIC1.GND, KF-1.ground, S1.Pin_1, S1.Pin_2, Mod1.-, LED1.cathode
  N3: Part1.D2, Mod1.Vin
  N4: Part1.D7, S1.Pin_3, S1.Pin_4
  N5: Part2.D21/SCL, LCM1602_IIC1.SCL
  N6: Part2.D20/SDA, LCM1602_IIC1.SDA
  N7: Part3.VBUS, LCM1602_IIC1.VCC, KF-1.power, KF-1.C, Mod1.S
  N8: F1.5V, KF-1.NO

custom parts:
  Adafruit Micro USB Breakout: Simple but effective - this breakout board has a USB Micro-B connector, with all 5 pins broken out. Great for pairing with a microcontroller with USB support, or adding USB 5V power to a project. We use a micro-AB connector with through-hole shielding pads for an excellent strong connection - it won't rip off by accident! Comes with one fully assembled and tested micro B breakout PCB and a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
  Fan - Ventilador: Ventilador de 2 pines, se encuentra comunmente en computadoras de escritorio
  LCM1602 IIC: I2C-Module to use a 1602 or 2004 LCD on with the wire.h libory Serial LCD Modul
  KF-301 Relay: KF-301
  KY-015 Temperature & Humidity Sensor Module: KY-015 temperature and humidity sensor module, provides a low-latency serial interface to measure humidity and temperature.
